# Fritzing sketch rage (saved by Fritzing 0.9.3b)
circuit board: 8.46667cm x 5.64444cm
breadboards: 1

parts:
  C1 = Electrolytic Capacitor [capacitance=1µF package="100 mil [THT, electrolytic]"]
  U2 = V_REG_LD1117VXX [package=78xxl]
  C2 = Electrolytic Capacitor [capacitance=1µF package="100 mil [THT, electrolytic]"]
  U3 = microSD Socket [package=usd-socket-pp]
  U4 = atmega328 [package=dip]
  R1 = Resistor [tolerance=±5% resistance=10k package=THT]
  R2 = Resistor [tolerance=±5% resistance=68 package=THT]
  U5 = 2.5mm Audio Jack [package=stereojack2.5mm_stereojack2.5mm]
  JP1 = Header 6 [package=molex-1x6_lock]

nets:
  GND: C1.-, U2.GND, C2.-, U3.SHIELD, U3.GND, U4.GND, U5.SLEEVE
  5V: C1.+, U2.IN
  VCC: U2.OUT, C2.+, U3.VCC, U4.VCC, U4.AVCC, U4.AREF, R1.Pin_0
  N1: U3.CS, U4.D4
  N2: U3.DI, U4.D11_(PWM)
  N3: U3.SCK, U4.D13
  N4: U3.DO, U4.D12
  N5: U4.RESET, R1.Pin_1
  N6: U4.D2, JP1.6
  N7: U4.D3_(PWM), R2.Pin_0
  N8: U4.D5_(PWM), JP1.5
  N9: U4.D6_(PWM), JP1.4
  N10: U4.D7, JP1.3
  N11: U4.D8, JP1.2
  N12: U4.D9_(PWM), JP1.1
  N13: R2.Pin_1, U5.LEFT
